// Logisim project RV32I_CPU.circ as structural Verilog
module PC (
  input  [31:0] next_pc,
  input  reset,
  input  clk,
  output [31:0] circuit_pc
);

  wire [31:0] multiplexer_1_out;

  Multiplexer #(.width(32)) multiplexer_1 (.in0(next_pc), .in1({32{1'b0}}), .out(multiplexer_1_out), .sel(reset));
  Register #(.width(32)) register_1 (.D(multiplexer_1_out), .en(1'b1), .clk(clk), .Q(circuit_pc));  // open: clr

  // Notes on the sheet:
  //   next_pc: initial=0x4
endmodule

module Register_File (
  input  [4:0] rs1,
  input  reg_write,
  input  [31:0] write_data,
  input  clk,
  input  [4:0] rd,
  input  [4:0] rs2,
  output [31:0] read_data1,
  output [31:0] read_data2
);

  wire and_1_out, and_2_out, and_3_out, and_4_out, and_5_out, and_6_out, and_7_out, and_8_out, and_9_out,
       and_10_out, and_11_out, and_12_out, and_13_out, and_14_out, and_15_out, and_16_out, and_17_out,
       and_18_out, and_19_out, and_20_out, and_21_out, and_22_out, and_23_out, and_24_out, and_25_out,
       and_26_out, and_27_out, and_28_out, and_29_out, and_30_out, and_31_out, decoder_1_out1,
       decoder_1_out2, decoder_1_out3, decoder_1_out4, decoder_1_out5, decoder_1_out6, decoder_1_out7,
       decoder_1_out8, decoder_1_out9, decoder_1_out10, decoder_1_out11, decoder_1_out12, decoder_1_out13,
       decoder_1_out14, decoder_1_out15, decoder_1_out16, decoder_1_out17, decoder_1_out18, decoder_1_out19,
       decoder_1_out20, decoder_1_out21, decoder_1_out22, decoder_1_out23, decoder_1_out24, decoder_1_out25,
       decoder_1_out26, decoder_1_out27, decoder_1_out28, decoder_1_out29, decoder_1_out30, decoder_1_out31;
  wire [31:0] x1_q, x2_q, x3_q, x4_q, x5_q, x6_q, x7_q, x8_q, x9_q, x10_q, x11_q, x12_q, x13_q, x14_q, x15_q,
       x16_q, x17_q, x18_q, x19_q, x20_q, x21_q, x22_q, x23_q, x24_q, x25_q, x26_q, x27_q, x28_q, x29_q,
       x30_q, x31_q;

  Decoder #(.select(5)) decoder_1 (
    .out1(decoder_1_out1), .out2(decoder_1_out2), .out3(decoder_1_out3), .out4(decoder_1_out4),
    .out5(decoder_1_out5), .out6(decoder_1_out6), .out7(decoder_1_out7), .out8(decoder_1_out8),
    .out9(decoder_1_out9), .out10(decoder_1_out10), .out11(decoder_1_out11), .out12(decoder_1_out12),
    .out13(decoder_1_out13), .out14(decoder_1_out14), .out15(decoder_1_out15), .out16(decoder_1_out16),
    .out17(decoder_1_out17), .out18(decoder_1_out18), .out19(decoder_1_out19), .out20(decoder_1_out20),
    .out21(decoder_1_out21), .out22(decoder_1_out22), .out23(decoder_1_out23), .out24(decoder_1_out24),
    .out25(decoder_1_out25), .out26(decoder_1_out26), .out27(decoder_1_out27), .out28(decoder_1_out28),
    .out29(decoder_1_out29), .out30(decoder_1_out30), .out31(decoder_1_out31), .sel(rd));  // open: out0, en
  and and_1 (and_1_out, reg_write, decoder_1_out1);
  and and_2 (and_2_out, reg_write, decoder_1_out2);
  and and_3 (and_3_out, reg_write, decoder_1_out3);
  and and_4 (and_4_out, reg_write, decoder_1_out4);
  and and_5 (and_5_out, reg_write, decoder_1_out5);
  and and_6 (and_6_out, reg_write, decoder_1_out6);
  and and_7 (and_7_out, reg_write, decoder_1_out7);
  and and_8 (and_8_out, reg_write, decoder_1_out8);
  and and_9 (and_9_out, reg_write, decoder_1_out9);
  and and_10 (and_10_out, reg_write, decoder_1_out10);
  and and_11 (and_11_out, reg_write, decoder_1_out11);
  and and_12 (and_12_out, reg_write, decoder_1_out12);
  and and_13 (and_13_out, reg_write, decoder_1_out13);
  and and_14 (and_14_out, reg_write, decoder_1_out14);
  and and_15 (and_15_out, reg_write, decoder_1_out15);
  and and_16 (and_16_out, reg_write, decoder_1_out16);
  and and_17 (and_17_out, reg_write, decoder_1_out17);
  and and_18 (and_18_out, reg_write, decoder_1_out18);
  and and_19 (and_19_out, reg_write, decoder_1_out19);
  and and_20 (and_20_out, reg_write, decoder_1_out20);
  and and_21 (and_21_out, reg_write, decoder_1_out21);
  and and_22 (and_22_out, reg_write, decoder_1_out22);
  and and_23 (and_23_out, reg_write, decoder_1_out23);
  and and_24 (and_24_out, reg_write, decoder_1_out24);
  and and_25 (and_25_out, reg_write, decoder_1_out25);
  and and_26 (and_26_out, reg_write, decoder_1_out26);
  and and_27 (and_27_out, reg_write, decoder_1_out27);
  and and_28 (and_28_out, reg_write, decoder_1_out28);
  and and_29 (and_29_out, reg_write, decoder_1_out29);
  and and_30 (and_30_out, reg_write, decoder_1_out30);
  and and_31 (and_31_out, reg_write, decoder_1_out31);
  Register #(.width(32)) x1 (.D(write_data), .en(and_1_out), .clk(clk), .Q(x1_q));  // open: clr
  Register #(.width(32)) x2 (.D(write_data), .en(and_2_out), .clk(clk), .Q(x2_q));  // open: clr
  Register #(.width(32)) x3 (.D(write_data), .en(and_3_out), .clk(clk), .Q(x3_q));  // open: clr
  Register #(.width(32)) x4 (.D(write_data), .en(and_4_out), .clk(clk), .Q(x4_q));  // open: clr
  Register #(.width(32)) x5 (.D(write_data), .en(and_5_out), .clk(clk), .Q(x5_q));  // open: clr
  Register #(.width(32)) x6 (.D(write_data), .en(and_6_out), .clk(clk), .Q(x6_q));  // open: clr
  Register #(.width(32)) x7 (.D(write_data), .en(and_7_out), .clk(clk), .Q(x7_q));  // open: clr
  Register #(.width(32)) x8 (.D(write_data), .en(and_8_out), .clk(clk), .Q(x8_q));  // open: clr
  Register #(.width(32)) x9 (.D(write_data), .en(and_9_out), .clk(clk), .Q(x9_q));  // open: clr
  Register #(.width(32)) x10 (.D(write_data), .en(and_10_out), .clk(clk), .Q(x10_q));  // open: clr
  Register #(.width(32)) x11 (.D(write_data), .en(and_11_out), .clk(clk), .Q(x11_q));  // open: clr
  Register #(.width(32)) x12 (.D(write_data), .en(and_12_out), .clk(clk), .Q(x12_q));  // open: clr
  Register #(.width(32)) x13 (.D(write_data), .en(and_13_out), .clk(clk), .Q(x13_q));  // open: clr
  Register #(.width(32)) x14 (.D(write_data), .en(and_14_out), .clk(clk), .Q(x14_q));  // open: clr
  Register #(.width(32)) x15 (.D(write_data), .en(and_15_out), .clk(clk), .Q(x15_q));  // open: clr
  Register #(.width(32)) x16 (.D(write_data), .en(and_16_out), .clk(clk), .Q(x16_q));  // open: clr
  Register #(.width(32)) x17 (.D(write_data), .en(and_17_out), .clk(clk), .Q(x17_q));  // open: clr
  Register #(.width(32)) x18 (.D(write_data), .en(and_18_out), .clk(clk), .Q(x18_q));  // open: clr
  Register #(.width(32)) x19 (.D(write_data), .en(and_19_out), .clk(clk), .Q(x19_q));  // open: clr
  Register #(.width(32)) x20 (.D(write_data), .en(and_20_out), .clk(clk), .Q(x20_q));  // open: clr
  Register #(.width(32)) x21 (.D(write_data), .en(and_21_out), .clk(clk), .Q(x21_q));  // open: clr
  Register #(.width(32)) x22 (.D(write_data), .en(and_22_out), .clk(clk), .Q(x22_q));  // open: clr
  Register #(.width(32)) x23 (.D(write_data), .en(and_23_out), .clk(clk), .Q(x23_q));  // open: clr
  Register #(.width(32)) x24 (.D(write_data), .en(and_24_out), .clk(clk), .Q(x24_q));  // open: clr
  Register #(.width(32)) x25 (.D(write_data), .en(and_25_out), .clk(clk), .Q(x25_q));  // open: clr
  Register #(.width(32)) x26 (.D(write_data), .en(and_26_out), .clk(clk), .Q(x26_q));  // open: clr
  Register #(.width(32)) x27 (.D(write_data), .en(and_27_out), .clk(clk), .Q(x27_q));  // open: clr
  Register #(.width(32)) x28 (.D(write_data), .en(and_28_out), .clk(clk), .Q(x28_q));  // open: clr
  Register #(.width(32)) x29 (.D(write_data), .en(and_29_out), .clk(clk), .Q(x29_q));  // open: clr
  Register #(.width(32)) x30 (.D(write_data), .en(and_30_out), .clk(clk), .Q(x30_q));  // open: clr
  Register #(.width(32)) x31 (.D(write_data), .en(and_31_out), .clk(clk), .Q(x31_q));  // open: clr
  Multiplexer #(.select(5), .width(32)) multiplexer_1 (
    .in0({32{1'b0}}), .in1(x1_q), .in2(x2_q), .in3(x3_q), .in4(x4_q), .in5(x5_q), .in6(x6_q), .in7(x7_q),
    .in8(x8_q), .in9(x9_q), .in10(x10_q), .in11(x11_q), .in12(x12_q), .in13(x13_q), .in14(x14_q),
    .in15(x15_q), .in16(x16_q), .in17(x17_q), .in18(x18_q), .in19(x19_q), .in20(x20_q), .in21(x21_q),
    .in22(x22_q), .in23(x23_q), .in24(x24_q), .in25(x25_q), .in26(x26_q), .in27(x27_q), .in28(x28_q),
    .in29(x29_q), .in30(x30_q), .in31(x31_q), .out(read_data1), .sel(rs1));
  Multiplexer #(.select(5), .width(32)) multiplexer_2 (
    .in0({32{1'b0}}), .in1(x1_q), .in2(x2_q), .in3(x3_q), .in4(x4_q), .in5(x5_q), .in6(x6_q), .in7(x7_q),
    .in8(x8_q), .in9(x9_q), .in10(x10_q), .in11(x11_q), .in12(x12_q), .in13(x13_q), .in14(x14_q),
    .in15(x15_q), .in16(x16_q), .in17(x17_q), .in18(x18_q), .in19(x19_q), .in20(x20_q), .in21(x21_q),
    .in22(x22_q), .in23(x23_q), .in24(x24_q), .in25(x25_q), .in26(x26_q), .in27(x27_q), .in28(x28_q),
    .in29(x29_q), .in30(x30_q), .in31(x31_q), .out(read_data2), .sel(rs2));
endmodule

module Imediate_Generator (
  input  [31:0] instruction,
  input  [2:0] imm_sel,
  output [31:0] imm_out
);

  wire [31:0] bit_extender_1_out, bit_extender_2_out, bit_extender_3_out, bit_extender_4_out;

  assign bit_extender_1_out = {{20{instruction[31]}}, instruction[31:20]};  // Bit_Extender bit_extender_1
  assign bit_extender_2_out = {{20{instruction[31]}}, {instruction[31:25], instruction[11:7]}};  // Bit_Extender bit_extender_2
  assign bit_extender_3_out = {{19{instruction[31]}}, {instruction[31], instruction[7], instruction[30:25], instruction[11:8], 1'b0}};  // Bit_Extender bit_extender_3
  assign bit_extender_4_out = {{11{instruction[31]}}, {instruction[31], instruction[19:12], instruction[20], instruction[30:21], 1'b0}};  // Bit_Extender bit_extender_4
  Multiplexer #(.select(3), .width(32)) multiplexer_1 (
    .in0(bit_extender_1_out), .in1(bit_extender_2_out), .in2(bit_extender_3_out),
    .in3({instruction[31:12], {12{1'b0}}}), .in4(bit_extender_4_out), .in5({32{1'b0}}), .in6({32{1'b0}}),
    .in7({32{1'b0}}), .out(imm_out), .sel(imm_sel));

  // Notes on the sheet:
  //   * 000 = I-type * 001 = S-type * 010 = B-type * 011 = U-type * 100 = J-type
endmodule

module Control_Unit (
  input  [6:0] opcode,
  output reg_write,
  output alu_src,
  output mem_write,
  output [1:0] alu_op,
  output mem_to_reg,
  output mem_read,
  output branch,
  output [2:0] imm_sel,
  output jump
);

  ROM #(.addrWidth(7), .dataWidth(12)) read_only_mem (
    .addr(opcode), .data({jump, imm_sel, branch, mem_read, mem_to_reg, alu_op, mem_write, alu_src, reg_write}));

  // Notes on the sheet:
  //   contents of read_only_mem (hex, n*v repeats v):
  //   0 0 0 63 15*0 13 0 0 0 319 11*0 106 15*0 11 0 0 0 319 43*0 288 0 0 0 803 7*0 c01
endmodule

module ALU_Control (
  input  [2:0] funct3,
  input  funct7_5,
  input  [1:0] alu_op,
  output [3:0] alu_ctrl
);

  ROM #(.addrWidth(6), .dataWidth(4)) read_only_memory (.addr({alu_op, funct7_5, funct3}), .data(alu_ctrl));

  // Notes on the sheet:
  //   contents of read_only_memory (hex, n*v repeats v):
  //   16*0 9*1 8*0 5 8 9 4 6 3 2 1 4*0 7 0 0 8*a
endmodule

module ALU (
  input  [31:0] b,
  input  [31:0] a,
  input  [3:0] alu_ctrl,
  output zero,
  output [31:0] result
);

  wire comparator_2_lt, comparator_3_lt;
  wire [31:0] add_result, and_result, or_result, sll_result, slr_result, slt_result, sltu_result, sra_result,
       srl_result, sub_result, xor_result;

  Comparator #(.mode("unsigned"), .width(32)) comparator_1 (.a(result), .b({32{1'b0}}), .eq(zero));  // open: gt, lt
  Comparator #(.width(32)) comparator_2 (.a(a), .b(b), .lt(comparator_2_lt));  // open: gt, eq
  Comparator #(.mode("unsigned"), .width(32)) comparator_3 (.a(a), .b(b), .lt(comparator_3_lt));  // open: gt, eq
  Adder #(.width(32)) adder_1 (.a(a), .b(b), .out(add_result));  // open: cin, cout
  Subtractor #(.width(32)) subtractor_1 (.a(a), .b(b), .out(sub_result));  // open: bin, bout
  assign and_result = a & b;  // AND_Gate and_1, 32 bits wide
  assign or_result = a | b;  // OR_Gate or_1, 32 bits wide
  assign xor_result = a ^ b;  // XOR_Gate xor_1, 32 bits wide
  Shifter #(.width(32)) shifter_1 (.in(a), .\dist (b[4:0]), .out(sll_result));
  Shifter #(.shift("lr"), .width(32)) shifter_2 (.in(a), .\dist (b[4:0]), .out(slr_result));
  Shifter #(.shift("ar"), .width(32)) shifter_3 (.in(a), .\dist (b[4:0]), .out(sra_result));
  assign slt_result = {{31{1'b0}}, comparator_2_lt};  // Bit_Extender bit_extender_1
  assign sltu_result = {{31{1'b0}}, comparator_3_lt};  // Bit_Extender bit_extender_2
  Multiplexer #(.select(4), .width(32)) multiplexer_1 (
    .in0(add_result), .in1(sub_result), .in2(and_result), .in3(or_result), .in4(xor_result),
    .in5(sll_result), .in6(srl_result), .in7(sra_result), .in8(slt_result), .in9(sltu_result), .in10(b),
    .in11({32{1'b0}}), .in12({32{1'b0}}), .in13({32{1'b0}}), .in14({32{1'b0}}), .in15({32{1'b0}}),
    .out(result), .sel(alu_ctrl));

  // Other names for the same wires on the sheet: lui_pass_result[31:0] = b; shamt[4:0] = b[4:0];
  //   result_internal[31:0] = result
endmodule

module Data_Memory (
  input  [2:0] funct3,
  input  [31:0] address,
  input  [31:0] write_data,
  input  mem_write,
  input  mem_read,
  input  clk,
  output [31:0] read_data
);

  wire or_1_out;
  wire [7:0] byte0, byte1, byte2, byte3, selected_byte;
  wire [15:0] selected_half;
  wire [31:0] and_1_out, and_2_out, lb_result, lbu_result, lh_result, lhu_result, merged_data, not_mask,
       sb_data, sb_mask, sh_data, sh_mask, shifted_wd, write_mask;

  // Probe on merged_data
  or or_1 (or_1_out, mem_write, mem_read);
  RAM #(.addrWidth(10), .dataWidth(32)) random_access_memory (
    .addr(address[11:2]), .we(mem_write), .oe(or_1_out), .clk(clk), .din(merged_data),
    .dout({byte3, byte2, byte1, byte0}));
  // Probe on {byte3, byte2, byte1, byte0}
  Multiplexer #(.select(2), .width(8)) multiplexer_1 (
    .in0(byte0), .in1(byte1), .in2(byte2), .in3(byte3), .out(selected_byte), .sel(address[1:0]));
  Multiplexer #(.width(16)) multiplexer_2 (
    .in0({byte1, byte0}), .in1({byte3, byte2}), .out(selected_half), .sel(address[1]));
  assign lb_result = {{24{selected_byte[7]}}, selected_byte};  // Bit_Extender bit_extender_1
  assign lbu_result = {{24{1'b1}}, selected_byte};  // Bit_Extender bit_extender_2
  assign lh_result = {{16{selected_half[15]}}, selected_half};  // Bit_Extender bit_extender_3
  assign lhu_result = {{16{1'b1}}, selected_half};  // Bit_Extender bit_extender_4
  // Probe on {byte3, byte2, byte1, byte0}
  // Probe on write_mask
  Multiplexer #(.select(2), .width(32)) multiplexer_3 (
    .in0({{24{1'b0}}, write_data[7:0]}), .in1({{16{1'b0}}, write_data[7:0], {8{1'b0}}}),
    .in2({{8{1'b0}}, write_data[7:0], {16{1'b0}}}), .in3({write_data[7:0], {24{1'b0}}}), .out(sb_data),
    .sel(address[1:0]));
  Multiplexer #(.select(2), .width(32)) multiplexer_4 (
    .in0(32'hff), .in1(32'hff00), .in2(32'hff0000), .in3(32'hff000000), .out(sb_mask), .sel(address[1:0]));
  Multiplexer #(.select(3), .width(32)) multiplexer_5 (
    .in0(sb_data), .in1(sh_data), .in2(write_data), .in3({32{1'b0}}), .in4({32{1'b0}}), .in5({32{1'b0}}),
    .in6({32{1'b0}}), .in7({32{1'b0}}), .out(shifted_wd), .sel(funct3));
  Multiplexer #(.select(3), .width(32)) multiplexer_6 (
    .in0(sb_mask), .in1(sh_mask), .in2({32{1'b1}}), .in3({32{1'b0}}), .in4({32{1'b0}}), .in5({32{1'b0}}),
    .in6({32{1'b0}}), .in7({32{1'b0}}), .out(write_mask), .sel(funct3));
  assign not_mask = ~write_mask;  // NOT_Gate not_1, 32 bits wide
  assign and_1_out = {byte3, byte2, byte1, byte0} & not_mask;  // AND_Gate and_1, 32 bits wide
  assign and_2_out = shifted_wd & write_mask;  // AND_Gate and_2, 32 bits wide
  Multiplexer #(.select(3), .width(32)) multiplexer_7 (
    .in0(lb_result), .in1(lh_result), .in2({byte3, byte2, byte1, byte0}), .in3({32{1'b0}}), .in4(lhu_result),
    .in5(lbu_result), .in6({32{1'b0}}), .in7({32{1'b0}}), .out(read_data), .sel(funct3));
  // Probe on not_mask
  assign merged_data = and_1_out | and_2_out;  // OR_Gate or_2, 32 bits wide
  Multiplexer #(.width(32)) multiplexer_8 (
    .in0({{16{1'b0}}, write_data[15:0]}), .in1({write_data[15:0], {16{1'b0}}}), .out(sh_data),
    .sel(address[1]));
  Multiplexer #(.width(32)) multiplexer_9 (.in0(32'hffff), .in1(32'hffff0000), .out(sh_mask), .sel(address[1]));

  // Other names for the same wires on the sheet: addr_bit0 = address[0]; addr_low2[1:0] = address[1:0];
  //   addr_bit1 = address[1]; word_addr[9:0] = address[11:2]; half0[15:0] = {byte1, byte0};
  //   ram_out[31:0] = {byte3, byte2, byte1, byte0}; half1[15:0] = {byte3, byte2}; wd_byte[7:0] = write_data[7:0];
  //   wd_byte_lane0[7:0] = write_data[7:0]; wd_byte_lane1[15:8] = write_data[7:0];
  //   wd_byte_lane2[23:16] = write_data[7:0]; wd_byte_lane3[31:24] = write_data[7:0];
  //   wd_half[15:0] = write_data[15:0]; wd_half_lane0[15:0] = write_data[15:0];
  //   wd_half_lane1[31:16] = write_data[15:0]
endmodule

module Branch_Comparator (
  input  [31:0] a,
  input  [31:0] b,
  input  [2:0] funct3,
  output branch_taken
);

  wire eq, ge_signed, ge_singed, ge_unsigned, lt_signed, lt_unsigned, ne;

  not not_1 (ge_singed, lt_signed);
  not not_2 (ne, eq);
  not not_3 (ge_unsigned, lt_unsigned);
  Comparator #(.width(32)) comparator_1 (.a(a), .b(b), .eq(eq), .lt(lt_signed));  // open: gt
  Comparator #(.mode("unsigned"), .width(32)) comparator_2 (.a(a), .b(b), .lt(lt_unsigned));  // open: gt, eq
  Multiplexer #(.select(3)) multiplexer_1 (
    .in0(eq), .in1(ne), .in2(1'b0), .in3(1'b0), .in4(lt_signed), .in5(ge_signed), .in6(lt_unsigned),
    .in7(ge_unsigned), .out(branch_taken), .sel(funct3));
endmodule

module CPU (
  input  reset,
  input  clk,
  output [31:0] pc_out
);

  wire alu_src, and_2_out, branch, branch_comparator_1_branch_taken, control_unit_1_mem_read,
       control_unit_1_mem_write, control_unit_1_reg_write, do_branch, is_branch_or_jal, is_jalr, jump,
       mem_to_reg, not_1_out, not_2_out;
  wire [0:0] adder_3_out, and_4_out;
  wire [1:0] control_unit_1_alu_op;
  wire [2:0] control_unit_1_imm_sel, funct3;
  wire [3:0] alu_control_1_alu_ctrl;
  wire [31:0] alu_result, bit_extender_1_out, imm_out, instruction, mem_data, multiplexer_1_out,
       multiplexer_2_out, multiplexer_3_out, pc_branch, pc_plus_4, rs1_val, rs2_val;
  wire [31:1] pc_jalr;

  Adder #(.width(32)) adder_1 (.a(pc_out), .b(32'h4), .out(pc_plus_4));  // open: cin, cout
  Adder #(.width(32)) adder_2 (.a(pc_out), .b(imm_out), .out(pc_branch));  // open: cin, cout
  Adder #(.width(32)) adder_3 (.a(rs1_val), .b(imm_out), .out({pc_jalr, adder_3_out[0]}));  // open: cin, cout
  PC pc_1 (.next_pc(multiplexer_1_out), .reset(reset), .clk(clk), .circuit_pc(pc_out));
  assign bit_extender_1_out = {{31{1'b0}}, 1'b0};  // Bit_Extender bit_extender_1
  not not_1 (not_1_out, instruction[3]);
  Multiplexer #(.select(2), .width(32)) multiplexer_1 (
    .in0(pc_plus_4), .in1(pc_branch), .in2({pc_jalr, 1'b0}), .in3(bit_extender_1_out),
    .out(multiplexer_1_out), .sel({is_jalr, is_branch_or_jal}));
  and and_1 (is_jalr, jump, not_1_out);
  and and_2 (and_2_out, jump, instruction[3]);
  Instruction_Memory instruction_memory_1 (
    .circuit_pc(pc_out), .instruction({instruction[31:15], funct3, instruction[11:0]}));
  or or_1 (is_branch_or_jal, and_2_out, do_branch);
  Control_Unit control_unit_1 (
    .opcode(instruction[6:0]), .reg_write(control_unit_1_reg_write), .alu_src(alu_src),
    .mem_write(control_unit_1_mem_write), .alu_op(control_unit_1_alu_op), .mem_to_reg(mem_to_reg),
    .mem_read(control_unit_1_mem_read), .branch(branch), .imm_sel(control_unit_1_imm_sel), .jump(jump));
  Imediate_Generator imediate_generator_1 (
    .instruction({instruction[31:15], funct3, instruction[11:0]}), .imm_sel(control_unit_1_imm_sel),
    .imm_out(imm_out));
  Register_File register_file_1 (
    .rs1(instruction[19:15]), .reg_write(control_unit_1_reg_write), .write_data(multiplexer_3_out),
    .clk(clk), .rd(instruction[11:7]), .rs2(instruction[24:20]), .read_data1(rs1_val), .read_data2(rs2_val));
  ALU_Control alu_control_1 (
    .funct3(funct3), .funct7_5(instruction[30]), .alu_op(control_unit_1_alu_op),
    .alu_ctrl(alu_control_1_alu_ctrl));
  Multiplexer #(.width(32)) multiplexer_2 (.in0(rs2_val), .in1(imm_out), .out(multiplexer_2_out), .sel(alu_src));
  ALU alu_1 (.b(multiplexer_2_out), .a(rs1_val), .alu_ctrl(alu_control_1_alu_ctrl), .result(alu_result));  // open: zero
  Branch_Comparator branch_comparator_1 (
    .a(rs1_val), .b(rs2_val), .funct3(funct3), .branch_taken(branch_comparator_1_branch_taken));
  and and_3 (do_branch, branch_comparator_1_branch_taken, branch);
  not not_2 (not_2_out, jump);
  Data_Memory data_memory_1 (
    .funct3(funct3), .address(alu_result), .write_data(rs2_val), .mem_write(control_unit_1_mem_write),
    .mem_read(control_unit_1_mem_read), .clk(clk), .read_data(mem_data));
  Multiplexer #(.select(2), .width(32)) multiplexer_3 (
    .in0(alu_result), .in1(mem_data), .in2(pc_plus_4), .in3({32{1'b0}}), .out(multiplexer_3_out),
    .sel({jump, and_4_out[0]}));
  and and_4 (and_4_out[0], not_2_out, mem_to_reg);

  // Other names for the same wires on the sheet: opcode[6:0] = instruction[6:0]; opcode_bit3 = instruction[3];
  //   instruction[14:12] = funct3; pc[31:0] = pc_out
endmodule

module Instruction_Memory (
  input  [31:0] circuit_pc,
  output [31:0] instruction
);

  ROM #(.dataWidth(32)) read_only_memory_block (.addr(circuit_pc[9:2]), .data(instruction));

  // Notes on the sheet:
  //   circuit_pc: initial=0x4
  //   contents of read_only_memory_block (hex, n*v repeats v):
  //   500093 708113 ffe10193 6f
endmodule
